# Fritzing sketch Esprinkler2V2 (saved by Fritzing 0.8.7b)
circuit board: 8.46667cm x 5.64444cm
breadboards: 1

parts:
  U1 = 74HC595 [package="DIP16 [THT]"]
  Q1 = NPN-Transistor [part_number=2n2222 package="TO92 [THT]"]
  R1 = Resistor [tolerance=±5% resistance=10k package=THT]
  WeMos_D1_Mini1 = WeMos D1 Mini
  K1 = RELAY [package=relay-g5q]
  K2 = RELAY [package=relay-g5q]
  Q2 = NPN-Transistor [part_number=2n2222 package="TO92 [THT]"]
  R2 = Resistor [tolerance=±5% resistance=10k package=THT]
  R3 = Resistor [tolerance=±5% resistance=220 package=THT]
  R4 = Resistor [tolerance=±5% resistance=220 package=THT]
  LED1 = LED - 5mm [color="Red (633nm)" package="5 mm [THT]"]
  LED2 = LED - 5mm [color="Red (633nm)" package="5 mm [THT]"]
  IC1 = DS1307 [package=THT]

nets:
  N1: U1.Q1, R2.Pin_1
  GND: U1.GND, U1.OE, Q1.E, WeMos_D1_Mini1.G, Q2.E, LED1.cathode, LED2.cathode, IC1.0V
  5V: U1.MR, U1.VCC, Q1.C, WeMos_D1_Mini1.5V, K1.COIL2, K1.COIL1, K2.COIL2, IC1.+V
  N2: U1.SH_CP, WeMos_D1_Mini1.D5
  N3: U1.ST_CP, WeMos_D1_Mini1.D8
  N4: U1.DS, WeMos_D1_Mini1.D7
  N5: U1.Q0, R1.Pin_1
  N6: Q1.B, R1.Pin_0
  N7: WeMos_D1_Mini1.D1, IC1.SCL_-_I2C_Clock
  N8: WeMos_D1_Mini1.D2, IC1.SDA_-_I2C_Data
  N9: WeMos_D1_Mini1.D3, R3.Pin_1
  N10: WeMos_D1_Mini1.D4, R4.Pin_1
  24vac: K1.MAIN, K2.MAIN
  N11: K1.NO, K2.NO
  Output 1: K1.NC
  Output 2: K2.NC
  N12: K2.COIL1, Q2.C
  N13: Q2.B, R2.Pin_0
  N14: R3.Pin_0, LED1.anode
  N15: R4.Pin_0, LED2.anode

notes:
  K3-K8, Q1-Q8, R1-R8
  all the same connected to Q2-Q7
  Illistration Purposes Only.
  ESPrinkler2
  0.1
  This schematic is intended as a general guide. DIY assembly and soldering skills are required to complete this project.
